# Fritzing sketch tempSensorThingsBoard_StandAlone (saved by Fritzing 0.9.3b)
circuit board: 4.27559cm x 1.65181cm
breadboards: 1

parts:
  U1 = ESP8266 WiFi Module [part_number=ESP8266]
  VCC1 = Battery
  DS1620 = IC, DIP package, 8 pins [chip_label=DS1620 part_number=DS1620]

nets:
  N1: U1.RXD, DS1620.pin2
  3.3V: U1.VCC, U1.CH_PD, VCC1.+, DS1620.pin8
  N2: U1.GPIO_0, DS1620.pin3
  N3: U1.GPIO_2, DS1620.pin1
  GND: U1.GND, VCC1.-, DS1620.pin4

notes:
  TempSensor_v1.0
  Kike Ramirez
  25.01.2018 - MIT License
  Vcc
  GND
  ThingsBoard Temperature Sensor, 1.0
  ThingsBoard Temperature Sensor
  PCB Design for a sensor node in ThingsBoard IOT Platform
  Kike Ramirez - MIT License
  23.01.2018

custom parts:
  ESP8266 WiFi Module: Generic WiFi Module based on the ESP8266 with onboard PCB antenna and UART communications
